# Fritzing sketch balcony (saved by Fritzing 0.9.2b)
breadboards: 1

parts:
  Part1 = Arduino Uno (Rev3)
  Part3 = Logic Level Converter
  Part2 = Breadboard Power Supply Board SMD
  RHT1 = Humidity and Temperature Sensor RHT03
  R1 = Resistor [tolerance=±5% resistance=10k package=THT]
  R2 = Resistor [tolerance=±5% resistance=100k package=THT]
  R3 = Resistor [tolerance=±5% resistance=100k package=THT]
  R4 = Resistor [tolerance=±5% resistance=100k package=THT]
  BAT1 = Battery Holders [package=battery-aa-kit]
  U1 = RELAY [package=relay-jzc]  # not connected
  ORP_Circuit1 = ORP Circuit
  R5 = Resistor [tolerance=±5% resistance=220 package=THT]
  C1 = Ceramic Capacitor [capacitance=100nF package="100 mil [THT, multilayer]"]
  C2 = Electrolytic Capacitor [capacitance=0.47mF package="100 mil [THT, electrolytic]"]
  C3 = Electrolytic Capacitor [capacitance=47µF package="100 mil [THT, electrolytic]"]

nets:
  N1: Part1.A1, R3.Pin_1, R4.Pin_0
  N2: Part1.D11_PWM/MOSI, RHT1.Data-signal, R1.Pin_1
  N3: Part1.D2, Part3.RX_HV
  N4: Part1.D3_PWM, Part3.RX2_HV
  N5: Part1.D4, Part3.TX2_HV
  N6: Part1.D6_PWM, R5.Pin_0, C1.1
  N7: Part1.D7, R5.Pin_1
  VCC: Part1.3V3, Part1.5V, Part3.LV, Part3.HV, Part2.VCC, RHT1.Vcc, R1.Pin_0, ORP_Circuit1.Vcc, C3.+
  GND: Part1.GND, Part3.GND, Part2.GND, RHT1.GND_2, R4.Pin_1, BAT1.-, ORP_Circuit1.PRB, C1.0, C2.-, C3.-
  N8: Part2.VIN, R2.Pin_0, BAT1.+, C2.+
  N9: R2.Pin_1, R3.Pin_0

notes:
  5V side
  3.3V side
  12V voltage divider
  12V7A battery
  to
  esp8266
  relays module
  * Vcc
  * GND
  * PIN
  moist sensor
  * Vcc
  * GND
  * DPIN
  * APIN
  capacitive water level sensor
